# Fritzing sketch sketch (saved by Fritzing 0.9.2b)

parts:
  Composant1 = Arduino Yun
  LED1 = smd LED [color="Red (633nm)" package="1206 [SMD]"]
  C1 = Electrolytic Capacitor [capacitance=1µF package="100 mil [THT, electrolytic]"]

nets:
  N1: Composant1.D13/SCK, LED1.anode
  N2: Composant1.GND, LED1.cathode
  N3: Composant1.D2, C1.-
  N4: Composant1.5V, C1.+
